# Fritzing sketch Arduino_ReadData (saved by Fritzing 0.8.3b)
breadboards: 1

parts:
  Part1 = Arduino Uno (Rev3)
  R1 = Resistor [tolerance=±5% resistance=1k package=THT]
  S1 = Pushbutton [package="[THT]"]
  R2 = Rotary Potentiometer (Small)
  R3 = Photocell (LDR) [package=THT]
  R4 = Resistor [tolerance=±5% resistance=220 package=THT]

nets:
  N1: Part1.A0, R1.Pin_1, R3.pin_0
  N2: Part1.A1, R2.wiper
  N3: Part1.GND, R1.Pin_0, R2.leg1, R2.leg2, R4.Pin_0
  N4: Part1.D8, Part1.5V, S1.Pin_1, S1.Pin_2, S1.Pin_3, S1.Pin_4, R3.pin_1, R4.Pin_1

notes:
  www.geekytheory.com
